# Fritzing sketch nitw-aws-relay-connection (saved by Fritzing 0.9.3b)

parts:
  Part1 = Arduino Uno (Rev3)
  KY-1 = Keyes Relay [package=THT]

nets:
  N1: Part1.D2, KY-1.signal
  N2: Part1.5V, KY-1.power
  N3: Part1.GND, KY-1.ground

custom parts:
  Keyes Relay: The Keyes 5V relay module is suitable for SCM development, home appliance control. It uses a 5V~12V TIL control signal which can control DC / AC signal.
